# Fritzing sketch Feather Canbus Shield V2.3 (saved by Fritzing 0.9.3b)
circuit board: 5.13077cm x 2.3cm
breadboards: 1

parts:
  Adafruit_Feather_32u4_Bluefruit_LE = Adafruit Feather 32u4 Bluefruit [part_number="Adafruit #2829"]
  MCP2515_I/P = MCP2515 [package=THT]
  MCP2551 = MCP2551 DIP - 8 pins [package="DIP (Dual Inline) [THT]"]
  16MHZ = Crystal [frequency="16 Mhz" package=THT]
  22pF = Capacitor [package=cap-pth-small]
  22pF_2 = Capacitor [package=cap-pth-small]
  CAN_JP = male pin header, 2 pins [form="♂ (male)"]
  120Ω = Resistor [tolerance=±1% resistance=120 package=THT]
  47kΩ = Resistor [tolerance=±5% resistance=47k package=THT]
  10kΩ = Resistor [tolerance=±5% resistance=10k package=THT]
  PWR = LED - 3mm [color="Red (633nm)" package="3 mm [THT]"]
  CAN_SPEED = male pin header, 2 pins [form="♂ (male)"]
  1kΩ = Resistor [tolerance=±5% resistance=1k package=THT]
  1kΩ_2 = Resistor [tolerance=±5% resistance=1k package=THT]
  100nF = Capacitor [package=1206]
  100nF_2 = Capacitor [package=1206]
  H_-_L = Screw terminal - 2 pins [package=THT]
  INT = LED - 3mm [color="Red (633nm)" package="3 mm [THT]"]

nets:
  N1: Adafruit_Feather_32u4_Bluefruit_LE.MISO, MCP2515_I/P.SO
  N2: Adafruit_Feather_32u4_Bluefruit_LE.MOSI, MCP2515_I/P.SI
  N3: Adafruit_Feather_32u4_Bluefruit_LE.SCK, MCP2515_I/P.SCK
  N4: Adafruit_Feather_32u4_Bluefruit_LE.A4, MCP2515_I/P.CS
  VSS: Adafruit_Feather_32u4_Bluefruit_LE.GND, MCP2515_I/P.Vss, MCP2551.VSS, 22pF.2, 22pF_2.1, 47kΩ.Pin_1, PWR.cathode, CAN_SPEED.pin2, 100nF.2, 100nF_2.2
  VDD: Adafruit_Feather_32u4_Bluefruit_LE.VBUS, MCP2515_I/P.Vdd, MCP2551.VDD, 10kΩ.Pin_0, 1kΩ.Pin_1, 1kΩ_2.Pin_1, 100nF.1, 100nF_2.1
  N5: Adafruit_Feather_32u4_Bluefruit_LE.6, CAN_SPEED.pin1
  N6: Adafruit_Feather_32u4_Bluefruit_LE.3, MCP2515_I/P.INT, INT.cathode
  N7: MCP2515_I/P.TXCAN, MCP2551.TXD
  N8: MCP2515_I/P.RXCAN, MCP2551.RXD
  N9: MCP2515_I/P.OSC2, 16MHZ.pin_1, 22pF.1
  N10: MCP2515_I/P.OSC1, 16MHZ.pin_0, 22pF_2.2
  N11: MCP2515_I/P.RESET, 10kΩ.Pin_1
  N12: MCP2551.CANL, 120Ω.Pin_1, H_-_L.0v_GND
  N13: MCP2551.CANH, CAN_JP.pin2, H_-_L.+12v
  N14: MCP2551.RS, 47kΩ.Pin_0
  N15: CAN_JP.pin1, 120Ω.Pin_0
  N16: PWR.anode, 1kΩ_2.Pin_0
  N17: 1kΩ.Pin_0, INT.anode

notes:
  •-• 100Kpbs
  • •-• PIN 1 (TX) INT3
  • • 500Kpbs
  James Tanner aka IAmOrion
  https://www.facebook.com/TheMeroving1an
  https://www.iamorion.co.uk
  CAN
  Version 2.3

custom parts:
  Adafruit Feather 32u4 Bluefruit: This is the Adafruit Feather 32u4 Bluefruit - our take on an 'all-in-one' Arduino-compatible + Bluetooth Low Energy with built in USB and battery charging. Its an Adafruit Feather 32u4 with a BTLE module, ready to rock! We have other boards in the Feather family, check'em out here. Bluetooth Low Energy is the hottest new low-power, 2.4GHz spectrum wireless protocol. In particular, its the only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
  MCP2515: MCP2515 CAN Controller with SPI Interface
  MCP2551 DIP - 8 pins: MCP2551 High-Speed CAN Transceiver
  Screw terminal - 2 pins: Screw terminal with 2 pins
